// Logisim project 13-01-22_govinda.circ as structural Verilog: 1 circuit, main circuit main
module main (
  input  [15:0] INSTRUCTION_INPUT,
  input  RUN,
  input  CLEAR,
  output [3:0] out_4
);

  wire _1_q, adder_1_out, AND_2_out, and_3_out, AND_out, CLOCK_out, comparator_1_eq, comparator_2_eq,
       comparator_3_eq, comparator_4_eq, comparator_5_eq, comparator_6_eq, comparator_7_eq, comparator_8_eq,
       decoder_1_out0, decoder_1_out1, decoder_1_out2, decoder_1_out3, decoder_1_out4, decoder_1_out5,
       decoder_1_out6, decoder_1_out7, demultiplexer_1_out0, demultiplexer_1_out1, demultiplexer_1_out2,
       demultiplexer_1_out3, demultiplexer_1_out4, not_1_out, not_2_out, not_3_out, OR_out, subtractor_1_out,
       subtractor_2_out;
  wire [2:0] _4_q, adder_2_out, IR_q_2, multiplexer_1_out;
  wire [3:0] MBR_q;
  wire [8:0] IR_q, MAR_2_q;
  wire [15:0] adder_3_out, adder_4_out, adder_5_out, and_4_out, demultiplexer_2_out0, demultiplexer_2_out1,
       divider_1_out, MAR_q, multiplexer_2_out, multiplexer_3_out, multiplier_1_out, not_4_out, or_2_out,
       PC_q, ram_1_data, ram_2_data, register_1_q, register_2_q, register_3_q, register_4_q, register_5_q,
       register_6_q, register_7_q, register_8_q, shifter_1_out, shifter_2_out, shifter_3_out, shifter_4_out,
       subtractor_3_out, subtractor_4_out, undriven;
  wire [15:4] MBR_q_2;

  Demultiplexer #(.select(3), .disabled(0), .enable("false")) demultiplexer_1 (
    .out0(demultiplexer_1_out0), .out1(demultiplexer_1_out1), .out2(demultiplexer_1_out2),
    .out3(demultiplexer_1_out3), .out4(demultiplexer_1_out4), .in(CLOCK_out), .sel(_4_q));  // open: out5, out6, out7
  Register #(.width(3)) _4 (.D(adder_2_out), .Q(_4_q), .clk(CLOCK_out));  // open: en, clr
  Comparator #(.width(3)) comparator_1 (.a(_4_q), .b(3'b100), .eq(comparator_1_eq));  // open: gt, lt
  Multiplexer #(.width(3), .disabled(0), .enable("false")) multiplexer_1 (
    .in0(3'b001), .in1(3'b100), .out(multiplexer_1_out), .sel(comparator_1_eq));
  Subtractor #(.width(1)) subtractor_1 (.a(1'b1), .b(adder_1_out), .out(subtractor_1_out));  // open: bin, bout
  Register #(.width(1)) _1 (.D(adder_1_out), .Q(_1_q), .clk(demultiplexer_1_out1));  // open: en, clr
  Adder #(.width(1)) adder_1 (.a(_1_q), .b(1'b1), .out(adder_1_out));  // open: cin, cout
  Clock CLOCK (.out(CLOCK_out));
  Subtractor #(.width(1)) subtractor_2 (.a(1'b1), .b(subtractor_1_out), .out(subtractor_2_out));  // open: bin, bout
  Adder #(.width(3)) adder_2 (.a(_4_q), .b(multiplexer_1_out), .out(adder_2_out));  // open: cin, cout
  not not_1 (not_1_out, comparator_1_eq);
  Register #(.width(16)) MAR (.D(PC_q), .en(subtractor_1_out), .Q(MAR_q), .clk(demultiplexer_1_out0));  // open: clr
  Register #(.width(9)) MAR_2 (.D(IR_q), .en(subtractor_2_out), .Q(MAR_2_q), .clk(demultiplexer_1_out2));  // open: clr
  not not_2 (not_2_out, RUN);
  Register #(.width(16)) register_1 (
    .D(multiplexer_3_out), .en(decoder_1_out0), .Q(register_1_q), .clk(demultiplexer_1_out4));  // open: clr
  Register #(.width(16)) register_2 (
    .D(multiplexer_3_out), .en(decoder_1_out7), .Q(register_2_q), .clk(demultiplexer_1_out4));  // open: clr
  Register #(.width(16)) PC (.D(adder_3_out), .en(_1_q), .Q(PC_q), .clk(demultiplexer_1_out1));  // open: clr
  RAM #(.addrWidth(9), .dataWidth(16), .bus("separate")) ram_1 (
    .addr(MAR_2_q), .din(demultiplexer_2_out1), .data(ram_1_data), .str(OR_out), .clk(demultiplexer_1_out3),
    .ld(not_3_out), .clr(CLEAR));  // open: sel
  not not_3 (not_3_out, OR_out);
  RAM #(.addrWidth(16), .dataWidth(16), .bus("separate")) ram_2 (
    .addr(MAR_q), .din(INSTRUCTION_INPUT), .data(ram_2_data), .str(not_2_out), .clk(demultiplexer_1_out1),
    .ld(RUN), .clr(CLEAR));  // open: sel
  Decoder #(.select(3), .disabled(0)) decoder_1 (
    .out0(decoder_1_out0), .out1(decoder_1_out1), .out2(decoder_1_out2), .out3(decoder_1_out3),
    .out4(decoder_1_out4), .out5(decoder_1_out5), .out6(decoder_1_out6), .out7(decoder_1_out7), .sel(IR_q_2),
    .en(not_1_out));
  Register #(.width(16)) register_3 (
    .D(multiplexer_3_out), .en(decoder_1_out1), .Q(register_3_q), .clk(demultiplexer_1_out4));  // open: clr
  Register #(.width(16)) register_4 (
    .D(multiplexer_3_out), .en(decoder_1_out6), .Q(register_4_q), .clk(demultiplexer_1_out4));  // open: clr
  Register #(.width(16)) IR (.D(ram_2_data), .Q({out_4, IR_q_2, IR_q}), .clk(demultiplexer_1_out1));  // open: en, clr
  Register #(.width(16)) register_5 (
    .D(multiplexer_3_out), .en(decoder_1_out2), .Q(register_5_q), .clk(demultiplexer_1_out4));  // open: clr
  Register #(.width(16)) register_6 (
    .D(multiplexer_3_out), .en(decoder_1_out5), .Q(register_6_q), .clk(demultiplexer_1_out4));  // open: clr
  Adder #(.width(16)) adder_3 (.a(16'h1), .b(PC_q), .out(adder_3_out));  // open: cin, cout
  Register #(.width(16)) MBR (.D(ram_1_data), .Q({MBR_q_2, MBR_q}), .clk(demultiplexer_1_out3));  // open: en, clr
  Register #(.width(16)) register_7 (
    .D(multiplexer_3_out), .en(decoder_1_out3), .Q(register_7_q), .clk(demultiplexer_1_out4));  // open: clr
  Register #(.width(16)) register_8 (
    .D(multiplexer_3_out), .en(decoder_1_out4), .Q(register_8_q), .clk(demultiplexer_1_out4));  // open: clr
  or OR (OR_out, and_3_out, AND_2_out);
  Multiplexer #(.select(3), .width(16), .disabled(0), .enable("false")) multiplexer_2 (
    .in0(register_1_q), .in1(register_3_q), .in2(register_5_q), .in3(register_7_q), .in4(register_8_q),
    .in5(register_6_q), .in6(register_4_q), .in7(register_2_q), .out(multiplexer_2_out), .sel(IR_q_2));
  Comparator #(.width(1)) comparator_2 (.a(out_4[3]), .b(1'b0), .eq(comparator_2_eq));  // open: gt, lt
  and AND (AND_out, comparator_2_eq, comparator_3_eq, comparator_4_eq);
  Comparator #(.width(1)) comparator_3 (.a(out_4[2]), .b(1'b0), .eq(comparator_3_eq));  // open: gt, lt
  Comparator #(.width(1)) comparator_4 (.a(out_4[1]), .b(1'b0), .eq(comparator_4_eq));  // open: gt, lt
  and AND_2 (AND_2_out, AND_out, out_4[0]);
  Demultiplexer #(.width(16), .disabled(0), .enable("false")) demultiplexer_2 (
    .out0(demultiplexer_2_out0), .out1(demultiplexer_2_out1), .in(multiplexer_2_out), .sel(AND_2_out));
  Comparator #(.width(1)) comparator_5 (.a(1'b1), .b(out_4[3]), .eq(comparator_5_eq));  // open: gt, lt
  Comparator #(.width(1)) comparator_6 (.a(1'b0), .b(out_4[2]), .eq(comparator_6_eq));  // open: gt, lt
  Comparator #(.width(1)) comparator_7 (.a(1'b1), .b(out_4[1]), .eq(comparator_7_eq));  // open: gt, lt
  Comparator #(.width(1)) comparator_8 (.a(1'b1), .b(out_4[0]), .eq(comparator_8_eq));  // open: gt, lt
  and and_3 (and_3_out, comparator_5_eq, comparator_6_eq, comparator_7_eq, comparator_8_eq);
  Adder #(.width(16)) adder_4 (.a(demultiplexer_2_out0), .b({MBR_q_2, MBR_q}), .out(adder_4_out));  // open: cin, cout
  Subtractor #(.width(16)) subtractor_3 (
    .a(demultiplexer_2_out0), .b({MBR_q_2, MBR_q}), .out(subtractor_3_out));  // open: bin, bout
  Multiplier #(.width(16)) multiplier_1 (
    .a(demultiplexer_2_out0), .b({MBR_q_2, MBR_q}), .out(multiplier_1_out));  // open: cin, cout
  Divider #(.width(16)) divider_1 (
    .a(demultiplexer_2_out0), .b({MBR_q_2, MBR_q}), .out(divider_1_out));  // open: upper, rem
  Adder #(.width(16)) adder_5 (.a(demultiplexer_2_out0), .b(16'h1), .out(adder_5_out));  // open: cin, cout
  Subtractor #(.width(16)) subtractor_4 (
    .a(demultiplexer_2_out0), .b(16'h1), .out(subtractor_4_out));  // open: bin, bout
  assign and_4_out = demultiplexer_2_out0 & {MBR_q_2, MBR_q};  // AND_Gate and_4, 16 bits wide
  assign or_2_out = demultiplexer_2_out0 | {MBR_q_2, MBR_q};  // OR_Gate or_2, 16 bits wide
  assign not_4_out = ~demultiplexer_2_out0;  // NOT_Gate not_4, 16 bits wide
  Shifter #(.width(16), .shift("lr")) shifter_1 (.in(demultiplexer_2_out0), .\dist (MBR_q), .out(shifter_1_out));
  Shifter #(.width(16)) shifter_2 (.in(demultiplexer_2_out0), .\dist (MBR_q), .out(shifter_2_out));
  Shifter #(.width(16), .shift("rr")) shifter_3 (.in(demultiplexer_2_out0), .\dist (MBR_q), .out(shifter_3_out));
  Shifter #(.width(16), .shift("rl")) shifter_4 (.in(demultiplexer_2_out0), .\dist (MBR_q), .out(shifter_4_out));
  Multiplexer #(.select(4), .width(16), .disabled(0), .enable("false")) multiplexer_3 (
    .in0({MBR_q_2, MBR_q}), .in1(undriven), .in2(adder_4_out), .in3(subtractor_3_out),
    .in4(multiplier_1_out), .in5(divider_1_out), .in6(adder_5_out), .in7(subtractor_4_out), .in8(and_4_out),
    .in9(or_2_out), .in10(not_4_out), .in11({MBR_q_2, MBR_q}), .in12(shifter_1_out), .in13(shifter_2_out),
    .in14(shifter_3_out), .in15(shifter_4_out), .out(multiplexer_3_out), .sel(out_4));
endmodule
